# Fritzing sketch smartPoulailler (saved by Fritzing 0.9.3b)
breadboards: 1

parts:
  Composant1 = Arduino Mega 2560 (Rev3)
  R1 = Resistor [tolerance=±5% resistance=220 package=THT]
  LED1 = LED - 5mm [color="Blue (430nm)" package="5 mm [THT]"]
  LED2 = LED - 5mm [color="Green (555nm)" package="5 mm [THT]"]
  LED3 = LED - 5mm [color="White (4500K)" package="5 mm [THT]"]
  LED4 = LED - 5mm [color="Green (555nm)" package="5 mm [THT]"]
  LED5 = LED - 5mm [color="Red (633nm)" package="5 mm [THT]"]
  R2 = Resistor [tolerance=±5% resistance=220 package=THT]
  R3 = Resistor [tolerance=±5% resistance=220 package=THT]
  R4 = Resistor [tolerance=±5% resistance=220 package=THT]
  R5 = Resistor [tolerance=±5% resistance=220 package=THT]
  S1 = Pushbutton [package="[THT]"]
  S2 = Pushbutton [package="[THT]"]
  R6 = Resistor [tolerance=±5% resistance=10k package=THT]
  R7 = Photocell (LDR) [package=THT]

nets:
  N1: Composant1.A0, R6.Pin_1, R7.pin_1
  N2: Composant1.D13_PWM, S1.Pin_1, S1.Pin_2
  N3: Composant1.D12_PWM, S2.Pin_1, S2.Pin_2
  N4: Composant1.3V3, LED1.anode, LED2.anode, LED3.anode, LED4.anode, LED5.anode, R7.pin_0
  N5: Composant1.GND, S1.Pin_3, S1.Pin_4, S2.Pin_3, S2.Pin_4, R6.Pin_0
  N6: Composant1.D2_PWM, R4.Pin_1
  N7: Composant1.D3_PWM, R5.Pin_1
  N8: Composant1.D4_PWM, R1.Pin_1
  N9: Composant1.D5_PWM, R2.Pin_1
  N10: Composant1.D6_PWM, R3.Pin_1
  N11: R1.Pin_0, LED1.cathode
  N12: LED2.cathode, R2.Pin_0
  N13: LED3.cathode, R3.Pin_0
  N14: LED4.cathode, R5.Pin_0
  N15: LED5.cathode, R4.Pin_0
